# Fritzing sketch l14_plantwatering_Final_completed (saved by Fritzing 0.9.9b)
breadboards: 1

parts:
  Argon1 = Particle Argon
  WATER_PUMP1 = water pump/motor  # not connected
  Relay1 = Relay - 6 pins [package="DIP (Dual Inline) [THT]"]
  R1 = Resistor [tolerance=±5% resistance=220 package="0402 [SMD]"]
  Q1 = PNP-Transistor [package="TO92 [THT]"]
  R2 = Resistor [tolerance=±5% resistance=2.2 package="0402 [SMD]"]
  M1 = BMP280
  OLED_I2C1 = OLED 128x64 I2C Monochrome Display
  Grove1 = Grove Dust Sensor
  Part1 = MQ-131 breakout
  Chirp!_Soil_Moisture_Sensor1 = Chirp! Soil Moisture Sensor v2.7.3

nets:
  3.3V: Argon1.3.3V, Relay1.VCC, Relay1.ON, R1.Pin_0, Q1.B, R2.Pin_1, M1.VIN, OLED_I2C1.VDD, Grove1.NC#1, Part1.DO, Chirp!_Soil_Moisture_Sensor1.Pin_1
  GND: Argon1.GND, Relay1.GND, M1.GND, OLED_I2C1.GND, Grove1.SIG, Part1.GND, Chirp!_Soil_Moisture_Sensor1.pin_5
  N1: Argon1.A1, Chirp!_Soil_Moisture_Sensor1.pin_3
  N2: Argon1.A2, Grove1.NC#5
  N3: Argon1.A3, Part1.VCC
  N4: Argon1.A4, Q1.C, R2.Pin_0
  N5: Argon1.SDA, M1.SDA, OLED_I2C1.SDA
  N6: Argon1.SCL, M1.SCL, OLED_I2C1.SCK
  N7: Relay1.IN, R1.Pin_1, Q1.E

custom parts:
  Particle Argon: The Argon is a powerful Wi-Fi enabled development board that can act as either a standalone Wi-Fi endpoint or Wi-Fi enabled gateway for Particle Mesh networks. It is based on the Nordic nRF52840 and has built-in battery charging circuitry so it’s easy to connect a Li-Po and deploy your local network in minutes. The Argon is great for connecting existing projects to the Particle Device Cloud or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
  water pump/motor: WATER PUMP BY ARDUBLOCKTR
  Relay - 6 pins: A DIP stand-in part for whatever IC you want. With 6 pins on a 900mil dual inline package (DIP) footprint.
  BMP280: Temperature Humidity Barometric presure Sensor, I2C
  Grove Dust Sensor: PPD42 Grove Dust Sensor
  MQ-131 breakout: SKU: 101282
