# Fritzing sketch midterm2_Pump (saved by Fritzing 0.9.9b)
breadboards: 1

parts:
  Argon1 = Particle Argon
  WATER_PUMP1 = water pump/motor  # not connected
  Relay1 = Relay - 6 pins [package="DIP (Dual Inline) [THT]"]
  R1 = Resistor [tolerance=±5% resistance=220 package="0402 [SMD]"]
  Q1 = PNP-Transistor [package="TO92 [THT]"]
  R2 = Resistor [tolerance=±5% resistance=2.2 package="0402 [SMD]"]
  M1 = BMP280
  OLED_I2C1 = OLED 128x64 I2C Monochrome Display

nets:
  3.3V: Argon1.3.3V, Relay1.VCC, Relay1.ON, R1.Pin_0, Q1.B, R2.Pin_1, M1.VIN
  GND: Argon1.GND, Relay1.GND, M1.GND, OLED_I2C1.GND
  N1: Argon1.RX, Q1.C, R2.Pin_0
  N2: Argon1.SDA, M1.SDA, OLED_I2C1.SDA
  N3: Argon1.SCL, M1.SCL, OLED_I2C1.SCK
  N4: Relay1.IN, R1.Pin_1, Q1.E

custom parts:
  Particle Argon: The Argon is a powerful Wi-Fi enabled development board that can act as either a standalone Wi-Fi endpoint or Wi-Fi enabled gateway for Particle Mesh networks. It is based on the Nordic nRF52840 and has built-in battery charging circuitry so it’s easy to connect a Li-Po and deploy your local network in minutes. The Argon is great for connecting existing projects to the Particle Device Cloud or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
  water pump/motor: WATER PUMP BY ARDUBLOCKTR
  Relay - 6 pins: A DIP stand-in part for whatever IC you want. With 6 pins on a 900mil dual inline package (DIP) footprint.
  BMP280: Temperature Humidity Barometric presure Sensor, I2C
